// Logisim project APB1.circ as structural Verilog: 2 circuits, main circuit task
module \task  (
  input  PSEL_Q1,
  input  PEN_Q0,
  input  TRAN_EN,
  input  PCLK,
  input  PWRITE,
  input  [7:0] PWDATA,
  input  presetn,
  input  paddr,
  output PREADY,
  output out_10,
  output out_11,
  output [7:0] PRDATA
);

  wire and_1_out, and_2_out, and_3_out, not_1_out, or_1_out;

  not not_1 (not_1_out, PEN_Q0);
  and and_1 (and_1_out, PSEL_Q1, TRAN_EN);
  and and_2 (and_2_out, PSEL_Q1, not_1_out);
  or or_1 (or_1_out, and_2_out, and_1_out, TRAN_EN);
  D_Flip_Flop d_ff_1 (.clk(PCLK), .D(and_2_out), .Q(out_10), .reset(presetn));  // open: Qn, preset, en
  D_Flip_Flop d_ff_2 (.clk(PCLK), .D(or_1_out), .Q(out_11), .reset(presetn));  // open: Qn, preset, en
  and and_3 (and_3_out, out_10, out_11, PWRITE);
  and and_4 (PREADY, out_10, out_11);
  Register register_1 (.D(PWDATA), .en(and_3_out), .Q(PRDATA), .clk(PCLK));  // open: clr

  // Notes on the sheet:
  //   D0
  //   D1
  //   PEN
  //   PSEL
  //   pen psel pw=1 
  //   then reg enable
endmodule

module fsm (
  input  PSEL_Q1,
  input  PEN_Q0,
  input  TRAN_EN,
  output out_4,
  output out_5
);

  wire and_1_out, clock_1_out, not_1_out, or_1_out;

  Clock clock_1 (.out(clock_1_out));
  not not_1 (not_1_out, PEN_Q0);
  and and_1 (and_1_out, PSEL_Q1, not_1_out);
  or or_1 (or_1_out, and_1_out, TRAN_EN);
  D_Flip_Flop d_ff_1 (.clk(clock_1_out), .D(and_1_out), .Q(out_4));  // open: Qn, preset, en, reset
  D_Flip_Flop d_ff_2 (.clk(clock_1_out), .D(or_1_out), .Q(out_5));  // open: Qn, preset, en, reset

  // Notes on the sheet:
  //   PCLK
  //   D0
  //   D1
endmodule
