// Logisim project Master_Slave_APB.circ as structural Verilog: 5 circuits, main circuit APB
module APB (
  input  [7:0] PWData,
  input  PSELECTx,
  input  PENABLE,
  input  PREADY,
  input  [1:0] PADDR,
  input  PReady_M,
  input  PRESETn,
  input  [7:0] PWData_2,
  input  PENABLE_2,
  input  PSELECTx_2,
  input  PRESETn_2,
  output [7:0] PRDATA,
  output [7:0] PRDATA_2
);

  wire and_1_out, and_2_out, and_3_out, decoder_1_out0, decoder_1_out1, decoder_1_out2, decoder_1_out3,
       not_1_out, PCLK_2_out, PCLK_out;
  wire [7:0] register_1_q, register_2_q, register_3_q, register_4_q;

  Clock PCLK (.out(PCLK_out));
  // Probe on PWData
  Clock PCLK_2 (.out(PCLK_2_out));
  Decoder #(.select(2)) decoder_1 (
    .out0(decoder_1_out0), .out1(decoder_1_out1), .out2(decoder_1_out2), .out3(decoder_1_out3), .sel(PADDR),
    .en(and_1_out));
  and and_1 (and_1_out, PSELECTx, PENABLE, PREADY);
  // Probe on PWData_2
  and and_2 (and_2_out, PENABLE_2, PSELECTx_2);
  Register register_1 (.D(PWData), .en(decoder_1_out0), .Q(register_1_q), .clk(PCLK_out), .clr(PRESETn));
  Register register_2 (.D(PWData), .en(decoder_1_out1), .Q(register_2_q), .clk(PCLK_out), .clr(PRESETn));
  Register register_3 (.D(PWData), .en(decoder_1_out2), .Q(register_3_q), .clk(PCLK_out), .clr(PRESETn));
  Register register_4 (.D(PWData), .en(decoder_1_out3), .Q(register_4_q), .clk(PCLK_out), .clr(PRESETn));
  Register register_5 (.D(PWData_2), .en(and_2_out), .Q(PRDATA_2), .clk(PCLK_2_out), .clr(PRESETn_2));
  // Probe on PRDATA_2
  not not_1 (not_1_out, PREADY);
  // Probe on PRDATA
  Multiplexer #(.select(2), .width(8)) multiplexer_1 (
    .in0(register_1_q), .in1(register_2_q), .in2(register_3_q), .in3(register_4_q), .out(PRDATA),
    .sel(PADDR), .en(and_3_out));
  and and_3 (and_3_out, not_1_out, PReady_M);
endmodule

module Handshake_MasterSlave (
  input  [7:0] PWData,
  input  PENABLE,
  input  PSEL,
  input  PWrite,
  input  [1:0] PADDR,
  input  PReady,
  input  in_7,
  output [7:0] PRDATA,
  output Valid_S
);

  wire and_1_out, and_2_out, decoder_1_out0, decoder_1_out1, decoder_1_out2, decoder_1_out3, not_1_out,
       PCLK_out;
  wire [7:0] register_1_q, register_2_q, register_3_q, register_4_q;

  Clock PCLK (.out(PCLK_out));
  // Probe on PWData
  Decoder #(.select(2)) decoder_1 (
    .out0(decoder_1_out0), .out1(decoder_1_out1), .out2(decoder_1_out2), .out3(decoder_1_out3), .sel(PADDR),
    .en(and_1_out));
  and and_1 (and_1_out, PENABLE, PSEL, PWrite);
  Register register_1 (.D(PWData), .en(decoder_1_out0), .Q(register_1_q), .clk(PCLK_out));  // open: clr
  Register register_2 (.D(PWData), .en(decoder_1_out1), .Q(register_2_q), .clk(PCLK_out));  // open: clr
  Register register_3 (.D(PWData), .en(decoder_1_out2), .Q(register_3_q), .clk(PCLK_out));  // open: clr
  Register register_4 (.D(PWData), .en(decoder_1_out3), .Q(register_4_q), .clk(PCLK_out));  // open: clr
  // Probe on PRDATA
  Multiplexer #(.select(2), .width(8)) multiplexer_1 (
    .in0(register_1_q), .in1(register_2_q), .in2(register_3_q), .in3(register_4_q), .out(PRDATA),
    .sel(PADDR), .en(and_2_out));
  and and_2 (and_2_out, not_1_out, PReady);
  not not_1 (not_1_out, PWrite);

  assign Valid_S = in_7;
endmodule

// APB
module Bridge (
  input  PCLK,
  input  Transaction,
  input  [7:0] PWData,
  input  PWrite,
  input  [1:0] PADDR,
  output P_EN,
  output P_SELx,
  output [7:0] PRDATA,
  output PR_W,
  output [1:0] PADDR_2
);

  wire and_1_out, and_2_out, and_3_out, and_4_out, and_5_out, and_6_out, and_7_out, not_1_out, not_2_out,
       not_3_out, not_4_out, or_1_out, or_2_out;

  // Probe on PWData
  D_Flip_Flop d_ff_1 (.clk(PCLK), .D(or_1_out), .Q(P_SELx));  // open: Qn, preset, en, reset
  D_Flip_Flop d_ff_2 (.clk(PCLK), .D(and_4_out), .Q(P_EN));  // open: Qn, preset, en, reset
  not not_1 (not_1_out, P_EN);
  not not_2 (not_2_out, P_EN);
  and and_1 (and_1_out, Transaction, not_3_out, not_4_out);
  not not_3 (not_3_out, P_SELx);
  not not_4 (not_4_out, P_EN);
  and and_2 (and_2_out, P_SELx, not_1_out);
  and and_3 (and_3_out, Transaction, P_SELx, P_EN);
  Register register_1 (.D(PWData), .en(and_7_out), .Q(PRDATA), .clk(PCLK));  // open: clr
  Register #(.width(1)) register_2 (.D(PWrite), .en(and_7_out), .Q(PR_W), .clk(PCLK));  // open: clr
  Register #(.width(2)) register_3 (.D(PADDR), .en(and_7_out), .Q(PADDR_2), .clk(PCLK));  // open: clr
  and and_4 (and_4_out, not_2_out, P_SELx);
  or or_1 (or_1_out, and_1_out, and_2_out, and_3_out);
  and and_5 (and_5_out, P_SELx, P_EN);
  and and_6 (and_6_out, ~P_SELx, ~P_EN);  // AND_Gate
  or or_2 (or_2_out, and_5_out, and_6_out);
  and and_7 (and_7_out, Transaction, or_2_out);
endmodule

module Slave (
  input  [7:0] PWData,
  input  PENABLE,
  input  PSEL,
  input  PWrite,
  input  [1:0] PADDR,
  input  PCLK,
  input  PReady,
  input  DATA_VALID,
  output [7:0] PRDATA,
  output Valid_S
);

  wire and_1_out, and_2_out, decoder_1_out0, decoder_1_out1, decoder_1_out2, decoder_1_out3, not_1_out;
  wire [7:0] register_1_q, register_2_q, register_3_q, register_4_q;

  // Probe on PWData
  Decoder #(.select(2)) decoder_1 (
    .out0(decoder_1_out0), .out1(decoder_1_out1), .out2(decoder_1_out2), .out3(decoder_1_out3), .sel(PADDR),
    .en(and_1_out));
  and and_1 (and_1_out, PENABLE, PSEL, PWrite);
  Register register_1 (.D(PWData), .en(decoder_1_out0), .Q(register_1_q), .clk(PCLK));  // open: clr
  Register register_2 (.D(PWData), .en(decoder_1_out1), .Q(register_2_q), .clk(PCLK));  // open: clr
  Register register_3 (.D(PWData), .en(decoder_1_out2), .Q(register_3_q), .clk(PCLK));  // open: clr
  Register register_4 (.D(PWData), .en(decoder_1_out3), .Q(register_4_q), .clk(PCLK));  // open: clr
  // Probe on PRDATA
  Multiplexer #(.select(2), .width(8)) multiplexer_1 (
    .in0(register_1_q), .in1(register_2_q), .in2(register_3_q), .in3(register_4_q), .out(PRDATA),
    .sel(PADDR), .en(and_2_out));
  and and_2 (and_2_out, not_1_out, PReady);
  not not_1 (not_1_out, PWrite);

  assign Valid_S = DATA_VALID;
endmodule

module Master (
  input  Transaction,
  input  [7:0] PWData,
  input  PR_W,
  input  [1:0] PADDR,
  input  PReady,
  output [7:0] PRDATA
);

  wire bridge_1_p_en, bridge_1_p_selx, bridge_1_pr_w, PCLK_out, register_1_q;
  wire [1:0] bridge_1_paddr_2;
  wire [7:0] bridge_1_prdata;

  Clock PCLK (.out(PCLK_out));
  // Probe on PWData
  Bridge bridge_1 (
    .PCLK(PCLK_out), .Transaction(Transaction), .PWData(PWData), .PWrite(PR_W), .PADDR(PADDR),
    .P_EN(bridge_1_p_en), .P_SELx(bridge_1_p_selx), .PRDATA(bridge_1_prdata), .PR_W(bridge_1_pr_w),
    .PADDR_2(bridge_1_paddr_2));
  Register #(.width(1)) register_1 (.D(PReady), .Q(register_1_q), .clk(PCLK_out));  // open: en, clr
  Slave slave_1 (
    .PWData(bridge_1_prdata), .PENABLE(bridge_1_p_en), .PSEL(bridge_1_p_selx), .PWrite(bridge_1_pr_w),
    .PADDR(bridge_1_paddr_2), .PCLK(PCLK_out), .PReady(register_1_q), .PRDATA(PRDATA));  // open: Valid_S, DATA_VALID
  // Probe on PRDATA

  // Notes on the sheet:
  //   R = 0 (Read Data) 
  //   W = 1 (Write Data) 
endmodule
