// Logisim project comm protocol custom.circ as structural Verilog
module Master (
  input  [7:0] in_1,
  input  R_W
);

  wire button_1_out, comparator_1_eq, shift_register_1_out, undriven;
  wire [7:0] counter_1_q;

  Button button_1 (.out(button_1_out));
  // Probe on counter_1_q
  Counter counter_1 (.Q(counter_1_q), .clk(button_1_out), .clr(comparator_1_eq));  // open: load, D, count, carry
  Comparator #(.mode("unsigned")) comparator_1 (.a(counter_1_q), .b(8'ha), .eq(comparator_1_eq));  // open: gt, lt
  Shift_Register shift_register_1 (
    .in(1'b0), .clk(button_1_out), .out(shift_register_1_out), .load(undriven), .d0(in_1[7]), .d1(in_1[6]),
    .d2(in_1[5]), .d3(in_1[4]), .d4(in_1[3]), .d5(in_1[2]), .d6(in_1[1]), .d7(in_1[0]));  // open: shift, clr, q0, q1, q2, q3, q4, q5, q6, q7
endmodule

module slave (
  input  [7:0] DATA_IN,
  input  Slave_Valid,
  input  Valid_M,
  input  R_W,
  input  ready_S,
  input  ready_M,
  input  Clock,
  input  [1:0] ADDR,
  output [7:0] DATA_OUT,
  output Valid_S
);

  wire and_1_out, and_2_out, decoder_1_out0, decoder_1_out1, decoder_1_out2, decoder_1_out3, not_1_out;
  wire [7:0] register_1_q, register_2_q, register_3_q, register_4_q;

  and and_1 (and_1_out, Valid_M, ready_S, R_W);
  Decoder #(.select(2), .disabled(0)) decoder_1 (
    .out0(decoder_1_out0), .out1(decoder_1_out1), .out2(decoder_1_out2), .out3(decoder_1_out3), .sel(ADDR),
    .en(and_1_out));
  Register register_1 (.D(DATA_IN), .en(decoder_1_out0), .Q(register_1_q), .clk(Clock));  // open: clr
  Register register_2 (.D(DATA_IN), .en(decoder_1_out1), .Q(register_2_q), .clk(Clock));  // open: clr
  Register register_3 (.D(DATA_IN), .en(decoder_1_out2), .Q(register_3_q), .clk(Clock));  // open: clr
  Register register_4 (.D(DATA_IN), .en(decoder_1_out3), .Q(register_4_q), .clk(Clock));  // open: clr
  Multiplexer #(.select(2), .width(8)) multiplexer_1 (
    .in0(register_1_q), .in1(register_2_q), .in2(register_3_q), .in3(register_4_q), .out(DATA_OUT),
    .sel(ADDR), .en(and_2_out));
  and and_2 (and_2_out, not_1_out, ready_M);
  not not_1 (not_1_out, ready_S);

  assign Valid_S = Slave_Valid;
endmodule

module APB_slave (
  input  TRANSACTION_EN,
  input  PCLK,
  input  PRESETn,
  input  PSELx,
  input  PENABLE,
  input  [1:0] PADDR,
  input  PWRITE,
  input  [7:0] PWDATA,
  input  Slave_READY,
  output [7:0] PRDATA,
  output PREADY
);

  wire and_1_out, and_2_out, decoder_1_out0, decoder_1_out1, decoder_1_out2, decoder_1_out3, not_1_out,
       not_2_out, register_1_q, register_2_q, register_3_q;
  wire [7:0] register_4_q, register_5_q, register_6_q, register_7_q;

  not not_1 (not_1_out, PRESETn);
  Register #(.width(1)) register_1 (.D(PSELx), .Q(register_1_q), .clk(PCLK), .clr(not_1_out));  // open: en
  Register #(.width(1)) register_2 (.D(PENABLE), .Q(register_2_q), .clk(PCLK), .clr(not_1_out));  // open: en
  Register #(.width(1)) register_3 (.D(register_2_q), .Q(register_3_q), .clk(PCLK), .clr(not_1_out));  // open: en
  and and_1 (and_1_out, register_3_q, register_1_q, PWRITE, Slave_READY);
  Decoder #(.select(2), .disabled(0)) decoder_1 (
    .out0(decoder_1_out0), .out1(decoder_1_out1), .out2(decoder_1_out2), .out3(decoder_1_out3), .sel(PADDR),
    .en(and_1_out));
  Register register_4 (.D(PWDATA), .en(decoder_1_out0), .Q(register_4_q), .clk(PCLK), .clr(not_1_out));
  Register register_5 (.D(PWDATA), .en(decoder_1_out1), .Q(register_5_q), .clk(PCLK), .clr(not_1_out));
  Register register_6 (.D(PWDATA), .en(decoder_1_out2), .Q(register_6_q), .clk(PCLK), .clr(not_1_out));
  Register register_7 (.D(PWDATA), .en(decoder_1_out3), .Q(register_7_q), .clk(PCLK), .clr(not_1_out));
  Multiplexer #(.select(2), .width(8)) multiplexer_1 (
    .in0(register_4_q), .in1(register_5_q), .in2(register_6_q), .in3(register_7_q), .out(PRDATA),
    .sel(PADDR), .en(and_2_out));
  and and_2 (and_2_out, not_2_out, Slave_READY);
  not not_2 (not_2_out, PWRITE);

  assign PREADY = Slave_READY;
endmodule
